# Fritzing sketch rotatey-cube (saved by Fritzing 0.9.3b)

parts:
  Composant1 = Arduino Nano (Rev3.0) (ICSP)
  GY1 = MPU-6050 Board GY-521 [form="♀ (female)" package=THT]
  Squix1 = OLED 0.96" 128x64 I2C SSD1306

nets:
  N1: Composant1.D2, GY1.pin8
  GND: Composant1.VIN, Composant1.GND, GY1.pin2, GY1.pin7, Squix1.GND
  5V: Composant1.RESET, Composant1.5V, GY1.pin1, Squix1.VCC
  N2: Composant1.A5, GY1.pin3, Squix1.SCL
  N3: Composant1.A4, GY1.pin4, Squix1.SCA

custom parts:
  MPU-6050 Board GY-521: Acelerometro y Giroscopio MPU-6050 Board GY-521
